# Fritzing sketch mobile-sense (saved by Fritzing 0.9.2b)

parts:
  Part1 = Arduino Due (Rev2b)
  THERMO1 = MAX31855 Breakout Board with Thermocouple
  THERMO2 = MAX31855 Breakout Board with Thermocouple
  THERMO3 = MAX31855 Breakout Board with Thermocouple
  Part2 = Arduino XBee Shield
  U1 = LIPO-2000mAh [package=lipo-2000]
  Part3 = PowerBoost 1000 Basic
  Part4 = Arduino MicroSD Shield
  GPS1 = Adafruit Ultimate GPS Breakout

nets:
  N1: Part1.D16/TX2, Part2.DIN
  N2: Part1.D17/RX2, Part2.DOUT
  N3: Part1.D18/TX1, Part4.D7
  N4: Part1.D19/RX1, Part4.CS
  N5: Part1.IOREF, THERMO2.Vin
  N6: Part1.5V, Part3.5.0V
  GND: Part1.GND, THERMO2.GND, U1.-, Part3.GND
  N7: Part1.D9_PWM, Part4.D9
  N8: Part1.D10_PWM/SS0, THERMO2.CS
  N9: Part1.D11_PWM, Part4.MOSI
  N10: Part1.D12_PWM, Part4.MISO
  N11: Part1.D13_PWM, Part4.SCK
  N12: Part1.D4_PWM/SS1, THERMO1.CS
  N13: Part1.D52, THERMO3.CS
  N14: U1.+, Part3.VBAT
  N15: Part4.N$32, GPS1.PPS
  N16: Part4.N$33, GPS1.VIN
  N17: Part4.N$58, GPS1.GND
  N18: Part4.N$59, GPS1.RX
  N19: Part4.N$84, GPS1.TX
  N20: Part4.N$85, GPS1.FIX
  N21: Part4.N$110, GPS1.VBAT
  N22: Part4.N$111, GPS1.EN
  N23: Part4.N$136, GPS1.3.3V

notes:
  This should actually be an
  Adafruit Powerboost 500 Shield.
  https://www.adafruit.com/products/2078
  This should actually be an Adafruit Ultimate GPS Logger Shield, rather than the horrible amalgamation visible above.
  https://www.adafruit.com/products/1272

custom parts:
  PowerBoost 1000 Basic: The PowerBoost 1000 is a little DC/DC boost converter module that can run from 1.8V batteries or higher, and convert the battery output to 5.2V DC for running your 5V projects. At its heart is a TPS61030 boost converter from TI. This boost converter chip has some really nice extras such as low battery detection, 4A internal switch, synchronous conversion, excellent efficiency, and 700KHz high-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
